// Logisim project cpu.circ as structural Verilog: 1 circuit, main circuit cpu
module cpu (
  input  clk,
  input  [31:0] Instruction,
  input  [31:0] MemReadData,
  output [31:0] MemAddress,
  output [31:0] ProgramCounter,
  output [31:0] ra,
  output [31:0] sp,
  output [31:0] t0,
  output [31:0] t1,
  output [31:0] t2,
  output [31:0] s0,
  output [31:0] s1,
  output [31:0] a0,
  output [3:0] MemWriteMask,
  output [31:0] MemWriteData
);

  wire ASel, BrEq, BrLt, BrUn, BSel, PCSel, RegWEn;
  wire [1:0] WBSel;
  wire [2:0] ImmSel;
  wire [3:0] ALUSel;
  wire [31:0] adder_1_out, adder_2_out, ALUResult, Immediate, LoadData, multiplexer_1_out, multiplexer_3_out,
       multiplexer_4_out, r1, r2, Stage2, WB;

  Adder #(.width(32)) adder_1 (.a(ProgramCounter), .b(32'h4), .out(adder_1_out));  // open: cin, cout
  Multiplexer #(.width(32)) multiplexer_1 (.in0(adder_1_out), .in1(ALUResult), .out(multiplexer_1_out), .sel(PCSel));
  Register #(.width(32)) PC (.D(multiplexer_1_out), .clk(clk), .Q(ProgramCounter));  // open: en, clr
  Register #(.width(32)) register_1 (.D(ProgramCounter), .clk(clk), .Q(Stage2));  // open: en, clr
  control_logic control_logic_1 (
    .Instruction(Instruction), .BrEq(BrEq), .BrLt(BrLt), .PCSel(PCSel), .RegWEn(RegWEn), .ImmSel(ImmSel),
    .BrUn(BrUn), .ASel(ASel), .BSel(BSel), .ALUSel(ALUSel), .WBSel(WBSel));  // open: MemWEn
  Adder #(.width(32)) adder_2 (.a(32'h4), .b(Stage2), .out(adder_2_out));  // open: cin, cout
  regfile regfile_1 (
    .ReadIndex1(Instruction[19:15]), .ReadIndex2(Instruction[24:20]), .WriteIndex(Instruction[11:7]),
    .WriteData(WB), .RegWEn(RegWEn), .clk(clk), .ra(ra), .sp(sp), .t0(t0), .t1(t1), .t2(t2), .s0(s0),
    .s1(s1), .a0(a0), .ReadData1(r1), .ReadData2(r2));
  imm_gen imm_gen_1 (.Instruction(Instruction), .Immediate(Immediate));  // open: ImmSel
  Multiplexer #(.select(2), .width(32)) multiplexer_2 (
    .in0(LoadData), .in1(ALUResult), .in2(adder_2_out), .out(WB), .sel(WBSel));  // open: in3
  Multiplexer #(.width(32)) multiplexer_3 (.in0(r1), .in1(Stage2), .out(multiplexer_3_out), .sel(ASel));
  Multiplexer #(.width(32)) multiplexer_4 (.in0(r2), .in1(Immediate), .out(multiplexer_4_out), .sel(BSel));
  alu alu_1 (.A(multiplexer_3_out), .B(multiplexer_4_out), .ALUSel(ALUSel), .ALUResult(ALUResult));
  branch_comp branch_comp_1 (.BrData1(r1), .BrData2(r2), .BrUn(BrUn), .BrEq(BrEq), .BrLt(BrLt));
  // partial_store partial_store_1: pin names not known
  partial_load partial_load_1 (.DataToReg(LoadData));  // open: Instruction, MemAddress, DataFromMem

  // Notes on the sheet:
  //   To IMEM
  //   IMEM (do **NOT** move this)
  //   From IMEM
  //   Inputs/Outputs for testing. Do **NOT** move these.
  //   It is OK to move the PC, RegFile, ALU, MEM, Branch Comp, Imm Gen, Partial Load, Partial Store and Control Logic to wherever is most convenient for you when constructing your CPU, and to delete this text
  //   To DMEM
  //   DMEM (do **NOT** move this)
  //   From DMEM
endmodule
